# Fritzing sketch role (saved by Fritzing 0.9.3b)
breadboards: 1

parts:
  Parça1 = Arduino Uno (Rev3)
  2_Channel_Relay1 = 2 Channel Power Relay
  R1 = Resistor [tolerance=±5% resistance=220 package=THT]
  R2 = Resistor [tolerance=±5% resistance=220 package=THT]
  S3 = Pushbutton [package=THT]
  S4 = Pushbutton [package=THT]

nets:
  N1: Parça1.D8, R1.Pin_0, S3.leg0
  N2: Parça1.D9_PWM, R2.Pin_0, S4.leg0
  N3: Parça1.D5_PWM, 2_Channel_Relay1.IN1
  N4: Parça1.5V, 2_Channel_Relay1.VCC#14, S3.leg1, S4.leg1
  N5: Parça1.GND, 2_Channel_Relay1.GND#11, R1.Pin_1, R2.Pin_1

custom parts:
  2 Channel Power Relay: A 2 channel power relay. The module operates at 5V.
