# Fritzing sketch sensorler (saved by Fritzing 0.9.3b)
breadboards: 1

parts:
  Parça1 = Arduino Uno (Rev3)
  TCRT1 = TCRT5000 sensor module [part_number=151608]  # not connected
  MQ-3_Sensor1 = MQ-3 Breakout Board
  LED1 = LED - 5mm [color="Red (633nm)" package="5 mm [THT]"]
  R1 = Resistor [tolerance=±5% resistance=220 package=THT]

nets:
  N1: Parça1.A1, MQ-3_Sensor1.AOUT
  N2: Parça1.D2, LED1.anode
  5V: Parça1.5V, MQ-3_Sensor1.5V
  N3: Parça1.GND, MQ-3_Sensor1.DOUT, R1.Pin_0
  N4: LED1.cathode, R1.Pin_1

custom parts:
  TCRT5000 sensor module: breakout board with TCRT5000
  MQ-3 Breakout Board: MQ-3 alcohol gas sensor breakout board. Input voltage is 5V. Sensor output is available in analog and digital.
