# Fritzing sketch servo (saved by Fritzing 0.9.3b)
breadboards: 1

parts:
  Parça1 = Arduino Uno (Rev3)
  SERVO1 = Tower Pro SG90 servo [part_number=101246]
  R1 = Resistor [tolerance=±5% resistance=10k package=THT]
  R2 = Resistor [tolerance=±5% resistance=10k package=THT]
  S1 = Pushbutton [package=THT]
  S2 = Pushbutton [package=THT]

nets:
  N1: Parça1.D11_PWM/MOSI, SERVO1.Signal
  GND: Parça1.GND, SERVO1.GND, R1.Pin_0, R2.Pin_0
  N2: Parça1.D2, R1.Pin_1, S1.leg1
  N3: Parça1.D4, R2.Pin_1, S2.leg1
  5V: Parça1.5V, SERVO1.+5V, S1.leg0, S2.leg0

custom parts:
  Tower Pro SG90 servo: Original file by John De Cristofaro http://www.adafruit.com/products/1449 Adafruit Feedback Servo (Small) Edited by: e-radionica.com 28/9/2015
